# Fritzing sketch Complete_Design (saved by Fritzing 0.9.3b)
circuit board: 17.6802cm x 9.23836cm
breadboards: 2

parts:
  U2 = TMP102 [package=sot563]
  M2 = SN65HVD230 CAN Bus transciever module [package=THT]
  M4 = SN65HVD230 CAN Bus transciever module [package=THT]
  Part3 = STM32F407G-DISC1
  M6 = DC Motor
  Mod2 = KY-021 Mini Magnetic Reed Switch Module [package="Breakout board"]
  M5 = fc-51 [package=THT]
  R3 = Rotary Potentiometer (Small) [maximum_resistance=10kΩ package=THT]
  Part2 = STM32F407G-DISC1
  IC2 = L293D [package=THT]
  VCC3 = 4 x AAA Battery Mount

nets:
  N1: U2.SCL, Part2.pin46
  N2: U2.GND, M2.pin_2, Mod2.S, Mod2.-, Part2.pin3, Part2.pin8, Part2.pin12, Part2.pin26, Part2.pin51, Part2.pin75, Part2.pin95, Part2.pin100
  VCC: U2.VCC, M2.pin_1, Mod2.Vin, Part2.pin53, Part2.pin78
  N3: U2.SDA, Part2.pin17, Part2.pin22
  N4: M2.pin_3, Part2.pin80, Part2.pin85
  N5: M2.pin_4, Part2.pin55, Part2.pin60
  N6: M2.pin_5, M4.pin_4, M4.pin_5, Part3.pin60
  N7: M2.pin_6, M4.pin_6
  N8: M4.pin_1, Part3.pin53, Part3.pin78, Part3.pin79, M5.pin3
  N9: M4.pin_2, Part3.pin1, Part3.pin25, Part3.pin26, Part3.pin51, Part3.pin75, Part3.pin100, M5.pin2, R3.wiper, IC2.0V, VCC3.-
  N10: M4.pin_3, Part3.pin85
  N11: Part3.pin6, Part3.pin7, R3.leg2
  N12: Part3.pin11, IC2.Enable_1
  N13: Part3.pin34, M5.pin1
  N14: Part3.pin52, Part3.pin77, R3.leg1, IC2.+V
  N15: Part3.pin56, IC2.In_2
  N16: Part3.pin57, Part3.pin58, IC2.In_1
  N17: M6.pin_1, IC2.Out_2_(_Controlled_by_Enable_1_)
  N18: M6.pin_2, IC2.Out_1_(_Controlled_by_Enable_1_)
  N19: IC2.+Vmotor, VCC3.+

custom parts:
  SN65HVD230 CAN Bus transciever module: Bus Transceiver SN65HVD230 CAN Communication Module, for Arduino.
  STM32F407G-DISC1: The STM32F4DISCOVERY Discovery kit allows users to easily develop applications with the STM32F407VG high-performance microcontroller with the Arm® Cortex®-M4 32-bit core. It includes everything required either for beginners or experienced users to get started quickly. Based on STM32F407VG, it includes an ST-LINK/V2-A embedded debug tool, one STMEMS digital accelerometer, one digital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
  KY-021 Mini Magnetic Reed Switch Module: KY-021 magnetic reed switch module. A reed switch is a magnetic sensor that is normally open and gets closed when exposed to a magnetic field.
