# Fritzing sketch N1+N2 (saved by Fritzing 0.9.3b)
breadboards: 1

parts:
  M2 = SN65HVD230 CAN Bus transciever module [package=THT]
  Part2 = STM32F407G-DISC1
  Motor_Driver1 = L293D [package=THT]
  Motor1 = DC Motor
  IR_Sensor1 = fc-51 [package=THT]
  R3 = Rotary Potentiometer (Small) [maximum_resistance=10kΩ package=THT]
  Power_Supply_(motor)1 = 4 x AAA Battery Mount
  STM32_Node_1_(N1)1 = STM32F407G-DISC1
  Temperature_Module = TMP102 [package=sot563]
  Reed_Switch_(M2)1 = KY-021 Mini Magnetic Reed Switch Module [package="Breakout board"]
  CAN_C2 = SN65HVD230 CAN Bus transciever module [package=THT]
  U3 = LuaNode32 / ESP32 [part_number=ESP32S-PIN30]

nets:
  N1: M2.pin_1, Part2.pin53, Part2.pin78, IR_Sensor1.pin3
  N2: M2.pin_2, Part2.pin1, Part2.pin25, Part2.pin26, Part2.pin50, Part2.pin51, Part2.pin75, Part2.pin76, Motor_Driver1.0V, IR_Sensor1.pin2, R3.wiper, Power_Supply_(motor)1.-, U3.GND
  N3: M2.pin_3, Part2.pin85
  N4: M2.pin_4, Part2.pin60
  N5: M2.pin_5, CAN_C2.pin_5
  N6: Part2.pin6, R3.leg2
  N7: Part2.pin11, Motor_Driver1.Enable_1
  N8: Part2.pin31, U3.RX0
  N9: Part2.pin34, IR_Sensor1.pin1
  N10: Part2.pin52, Part2.pin77, Motor_Driver1.+V, R3.leg1
  N11: Part2.pin56, Motor_Driver1.In_2
  N12: Part2.pin57, Motor_Driver1.In_1
  N13: Part2.pin94, U3.TX0
  N14: Motor_Driver1.Out_1_(_Controlled_by_Enable_1_), Motor1.pin_2
  N15: Motor_Driver1.Out_2_(_Controlled_by_Enable_1_), Motor1.pin_1
  N16: Motor_Driver1.+Vmotor, Power_Supply_(motor)1.+
  N17: STM32_Node_1_(N1)1.pin8, Reed_Switch_(M2)1.S
  N18: STM32_Node_1_(N1)1.pin22, Temperature_Module.SDA
  N19: STM32_Node_1_(N1)1.pin25, STM32_Node_1_(N1)1.pin26, STM32_Node_1_(N1)1.pin51, STM32_Node_1_(N1)1.pin75, STM32_Node_1_(N1)1.pin100, Temperature_Module.GND, Reed_Switch_(M2)1.-, CAN_C2.pin_2
  N20: STM32_Node_1_(N1)1.pin46, Temperature_Module.SCL
  VCC: STM32_Node_1_(N1)1.pin53, STM32_Node_1_(N1)1.pin78, Temperature_Module.VCC, Reed_Switch_(M2)1.Vin, CAN_C2.pin_1
  N21: STM32_Node_1_(N1)1.pin60, CAN_C2.pin_4
  N22: STM32_Node_1_(N1)1.pin85, CAN_C2.pin_3

custom parts:
  SN65HVD230 CAN Bus transciever module: Bus Transceiver SN65HVD230 CAN Communication Module, for Arduino.
  STM32F407G-DISC1: The STM32F4DISCOVERY Discovery kit allows users to easily develop applications with the STM32F407VG high-performance microcontroller with the Arm® Cortex®-M4 32-bit core. It includes everything required either for beginners or experienced users to get started quickly. Based on STM32F407VG, it includes an ST-LINK/V2-A embedded debug tool, one STMEMS digital accelerometer, one digital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
  KY-021 Mini Magnetic Reed Switch Module: KY-021 magnetic reed switch module. A reed switch is a magnetic sensor that is normally open and gets closed when exposed to a magnetic field.
  LuaNode32 / ESP32: New Image for LuaNode32 DOIT ESP32 DEVKIT V1. Base parts from LuaNode32 / ESP32 ESP32 based LuaNode32 by G.Noorlander DOIT Esp32 DevKit v1 (30 pins long, 11 pins width) by Werner Rothschopf (modified by vanepp Dec 2018)
