# Fritzing sketch Node_1 (saved by Fritzing 0.9.3b)
breadboards: 1

parts:
  Temperature_Module_(M1) = TMP102 [package=sot563]
  Reed_Switch_(M2) = KY-021 Mini Magnetic Reed Switch Module [package="Breakout board"]
  CAN_C1 = SN65HVD230 CAN Bus transciever module [package=THT]
  STM32_Node_1_(N1) = STM32F407G-DISC1

nets:
  N1: Temperature_Module_(M1).SCL, STM32_Node_1_(N1).pin46
  N2: Temperature_Module_(M1).GND, Reed_Switch_(M2).-, CAN_C1.pin_2, STM32_Node_1_(N1).pin25, STM32_Node_1_(N1).pin51, STM32_Node_1_(N1).pin75, STM32_Node_1_(N1).pin76
  VCC: Temperature_Module_(M1).VCC, Reed_Switch_(M2).Vin, CAN_C1.pin_1, STM32_Node_1_(N1).pin53, STM32_Node_1_(N1).pin78
  N3: Temperature_Module_(M1).SDA, STM32_Node_1_(N1).pin22
  N4: Reed_Switch_(M2).S, STM32_Node_1_(N1).pin8
  N5: CAN_C1.pin_3, STM32_Node_1_(N1).pin85
  N6: CAN_C1.pin_4, STM32_Node_1_(N1).pin60

custom parts:
  KY-021 Mini Magnetic Reed Switch Module: KY-021 magnetic reed switch module. A reed switch is a magnetic sensor that is normally open and gets closed when exposed to a magnetic field.
  SN65HVD230 CAN Bus transciever module: Bus Transceiver SN65HVD230 CAN Communication Module, for Arduino.
  STM32F407G-DISC1: The STM32F4DISCOVERY Discovery kit allows users to easily develop applications with the STM32F407VG high-performance microcontroller with the Arm® Cortex®-M4 32-bit core. It includes everything required either for beginners or experienced users to get started quickly. Based on STM32F407VG, it includes an ST-LINK/V2-A embedded debug tool, one STMEMS digital accelerometer, one digital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
