# Fritzing sketch Node_2 (saved by Fritzing 0.9.3b)
breadboards: 1

parts:
  Part1 = STM32F407G-DISC1
  M1 = SN65HVD230 CAN Bus transciever module [package=THT]
  Motor_Driver = L293D [package=THT]
  IR_Sensor = fc-51 [package=THT]
  R2 = Rotary Potentiometer (Small) [maximum_resistance=10kΩ package=THT]
  Motor = DC Motor
  Power_Supply_(motor) = 4 x AAA Battery Mount
  U2 = LuaNode32 / ESP32 [part_number=ESP32S-PIN30]

nets:
  N1: Part1.pin1, Part1.pin25, Part1.pin26, Part1.pin50, Part1.pin51, Part1.pin75, M1.pin_2, Motor_Driver.0V, IR_Sensor.pin2, R2.wiper, Power_Supply_(motor).-, U2.GND
  N2: Part1.pin6, R2.leg2
  N3: Part1.pin11, Motor_Driver.Enable_1
  N4: Part1.pin31, U2.RX0
  N5: Part1.pin34, IR_Sensor.pin1
  N6: Part1.pin52, Part1.pin77, Motor_Driver.+V, R2.leg1
  N7: Part1.pin53, Part1.pin78, M1.pin_1, IR_Sensor.pin3
  N8: Part1.pin56, Motor_Driver.In_2
  N9: Part1.pin57, Motor_Driver.In_1
  N10: Part1.pin60, M1.pin_4
  N11: Part1.pin85, M1.pin_3
  N12: Part1.pin94, U2.TX0
  N13: Motor_Driver.Out_1_(_Controlled_by_Enable_1_), Motor.pin_2
  N14: Motor_Driver.Out_2_(_Controlled_by_Enable_1_), Motor.pin_1
  N15: Motor_Driver.+Vmotor, Power_Supply_(motor).+

custom parts:
  STM32F407G-DISC1: The STM32F4DISCOVERY Discovery kit allows users to easily develop applications with the STM32F407VG high-performance microcontroller with the Arm® Cortex®-M4 32-bit core. It includes everything required either for beginners or experienced users to get started quickly. Based on STM32F407VG, it includes an ST-LINK/V2-A embedded debug tool, one STMEMS digital accelerometer, one digital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
  SN65HVD230 CAN Bus transciever module: Bus Transceiver SN65HVD230 CAN Communication Module, for Arduino.
  LuaNode32 / ESP32: New Image for LuaNode32 DOIT ESP32 DEVKIT V1. Base parts from LuaNode32 / ESP32 ESP32 based LuaNode32 by G.Noorlander DOIT Esp32 DevKit v1 (30 pins long, 11 pins width) by Werner Rothschopf (modified by vanepp Dec 2018)
